// Logisim project CPU.circ as structural Verilog: 4 circuits, main circuit implementation
module implementation (
  input  [15:0] Instruction_In,
  input  ClkIn,
  output [4:0] Instruction_Address_Out,
  output [3:0] Reg0_Out,
  output [3:0] Reg1_Out,
  output [3:0] Reg2_Out,
  output [3:0] Reg3_Out,
  output [3:0] Reg4_Out,
  output [3:0] Reg5_Out,
  output [3:0] Reg6_Out,
  output [3:0] Reg7_Out,
  output [3:0] Reg8_Out,
  output [3:0] Reg9_Out,
  output [3:0] Reg10_Out,
  output [3:0] Reg11_Out,
  output [3:0] Reg12_Out,
  output [3:0] Reg13_Out,
  output [3:0] Reg14_Out,
  output [3:0] Reg15_Out
);

  wire Imm, IsImm, RegWrite, WriteEnable;
  wire [3:0] A_Value, B_Value, multiplexer_3_out, ResultALU;

  Multiplexer #(.enable("false")) multiplexer_1 (.in0(1'b0), .in1(1'b1), .out(RegWrite), .sel(WriteEnable));
  Multiplexer #(.enable("false"), .select(4)) multiplexer_2 (
    .in0(1'b0), .in1(1'b0), .in2(1'b1), .in3(1'b0), .in4(1'b0), .in5(1'b1), .in6(1'b0), .in7(1'b1),
    .in8(1'b0), .in9(1'b1), .in10(1'b0), .in11(1'b0), .in12(1'b0), .in13(1'b1), .in14(1'b0), .in15(1'b1),
    .out(Imm), .sel(Instruction_In[15:12]));
  PC pc_1 (
    .in_1(Instruction_In[15:12]), .in_2(ClkIn), .out_3(WriteEnable), .out_4(Instruction_Address_Out),
    .out_5(IsImm));
  Multiplexer #(.enable("false"), .width(4)) multiplexer_3 (
    .in0(B_Value), .in1(Instruction_In[3:0]), .out(multiplexer_3_out), .sel(IsImm));
  ALU alu_1 (.in_1(Instruction_In[15:12]), .in_2(A_Value), .in_3(multiplexer_3_out), .out_4(ResultALU));
  RegFile regfile_1 (
    .A_Sel_In(Instruction_In[7:4]), .B_Sel_In(Instruction_In[3:0]), .C_Sel_In(Instruction_In[11:8]),
    .Data_In(ResultALU), .Reg_Write_In(RegWrite), .clk_in(ClkIn), .A_Out(A_Value), .B_Out(B_Value),
    .Reg0_Out(Reg0_Out), .Reg1_Out(Reg1_Out), .Reg2_Out(Reg2_Out), .Reg3_Out(Reg3_Out), .Reg4_Out(Reg4_Out),
    .Reg5_Out(Reg5_Out), .Reg6_Out(Reg6_Out), .Reg7_Out(Reg7_Out), .Reg8_Out(Reg8_Out), .Reg9_Out(Reg9_Out),
    .Reg10_Out(Reg10_Out), .Reg11_Out(Reg11_Out), .Reg12_Out(Reg12_Out), .Reg13_Out(Reg13_Out),
    .Reg14_Out(Reg14_Out), .Reg15_Out(Reg15_Out));

  // Other names for the same wires on the sheet: Clk = ClkIn; BSelImm[3:0] = Instruction_In[3:0];
  //   Instruction[15:0] = Instruction_In; ASelIn[3:0] = Instruction_In[7:4]; CSelIn[3:0] = Instruction_In[11:8];
  //   Opcode[3:0] = Instruction_In[15:12]; Instruction_Address[4:0] = Instruction_Address_Out; Reg0[3:0] = Reg0_Out;
  //   Reg1[3:0] = Reg1_Out; Reg2[3:0] = Reg2_Out; Reg3[3:0] = Reg3_Out; Reg4[3:0] = Reg4_Out; Reg5[3:0] = Reg5_Out;
  //   Reg6[3:0] = Reg6_Out; Reg7[3:0] = Reg7_Out; Reg8[3:0] = Reg8_Out; Reg9[3:0] = Reg9_Out; Reg10[3:0] = Reg10_Out;
  //   Reg11[3:0] = Reg11_Out; Reg12[3:0] = Reg12_Out; Reg13[3:0] = Reg13_Out; Reg14[3:0] = Reg14_Out;
  //   Reg15[3:0] = Reg15_Out

  // Notes on the sheet:
  //   Done by Muskan Kumar
endmodule

module RegFile (
  input  [3:0] A_Sel_In,
  input  [3:0] B_Sel_In,
  input  [3:0] C_Sel_In,
  input  [3:0] Data_In,
  input  Reg_Write_In,
  input  clk_in,
  output [3:0] A_Out,
  output [3:0] B_Out,
  output [3:0] Reg0_Out,
  output [3:0] Reg1_Out,
  output [3:0] Reg2_Out,
  output [3:0] Reg3_Out,
  output [3:0] Reg4_Out,
  output [3:0] Reg5_Out,
  output [3:0] Reg6_Out,
  output [3:0] Reg7_Out,
  output [3:0] Reg8_Out,
  output [3:0] Reg9_Out,
  output [3:0] Reg10_Out,
  output [3:0] Reg11_Out,
  output [3:0] Reg12_Out,
  output [3:0] Reg13_Out,
  output [3:0] Reg14_Out,
  output [3:0] Reg15_Out
);

  wire Reg_Write0, Reg_Write1, Reg_Write2, Reg_Write3, Reg_Write4, Reg_Write5, Reg_Write6, Reg_Write7,
       Reg_Write8, Reg_Write9, Reg_Write10, Reg_Write11, Reg_Write12, Reg_Write13, Reg_Write14, Reg_Write15;

  Demultiplexer #(.enable("false"), .select(4)) demultiplexer_1 (
    .out0(Reg_Write0), .out1(Reg_Write1), .out2(Reg_Write2), .out3(Reg_Write3), .out4(Reg_Write4),
    .out5(Reg_Write5), .out6(Reg_Write6), .out7(Reg_Write7), .out8(Reg_Write8), .out9(Reg_Write9),
    .out10(Reg_Write10), .out11(Reg_Write11), .out12(Reg_Write12), .out13(Reg_Write13), .out14(Reg_Write14),
    .out15(Reg_Write15), .in(Reg_Write_In), .sel(C_Sel_In));
  Register #(.width(4)) register_1 (.D(Data_In), .en(Reg_Write0), .clk(clk_in), .Q(Reg0_Out));  // open: clr
  Register #(.width(4)) register_2 (.D(Data_In), .en(Reg_Write4), .clk(clk_in), .Q(Reg4_Out));  // open: clr
  Register #(.width(4)) register_3 (.D(Data_In), .en(Reg_Write8), .clk(clk_in), .Q(Reg8_Out));  // open: clr
  Register #(.width(4)) register_4 (.D(Data_In), .en(Reg_Write12), .clk(clk_in), .Q(Reg12_Out));  // open: clr
  Register #(.width(4)) register_5 (.D(Data_In), .en(Reg_Write1), .clk(clk_in), .Q(Reg1_Out));  // open: clr
  Register #(.width(4)) register_6 (.D(Data_In), .en(Reg_Write5), .clk(clk_in), .Q(Reg5_Out));  // open: clr
  Register #(.width(4)) register_7 (.D(Data_In), .en(Reg_Write9), .clk(clk_in), .Q(Reg9_Out));  // open: clr
  Register #(.width(4)) register_8 (.D(Data_In), .en(Reg_Write13), .clk(clk_in), .Q(Reg13_Out));  // open: clr
  Register #(.width(4)) register_9 (.D(Data_In), .en(Reg_Write2), .clk(clk_in), .Q(Reg2_Out));  // open: clr
  Register #(.width(4)) register_10 (.D(Data_In), .en(Reg_Write6), .clk(clk_in), .Q(Reg6_Out));  // open: clr
  Register #(.width(4)) register_11 (.D(Data_In), .en(Reg_Write10), .clk(clk_in), .Q(Reg10_Out));  // open: clr
  Register #(.width(4)) register_12 (.D(Data_In), .en(Reg_Write14), .clk(clk_in), .Q(Reg14_Out));  // open: clr
  Register #(.width(4)) register_13 (.D(Data_In), .en(Reg_Write3), .clk(clk_in), .Q(Reg3_Out));  // open: clr
  Register #(.width(4)) register_14 (.D(Data_In), .en(Reg_Write7), .clk(clk_in), .Q(Reg7_Out));  // open: clr
  Register #(.width(4)) register_15 (.D(Data_In), .en(Reg_Write11), .clk(clk_in), .Q(Reg11_Out));  // open: clr
  Register #(.width(4)) register_16 (.D(Data_In), .en(Reg_Write15), .clk(clk_in), .Q(Reg15_Out));  // open: clr
  Multiplexer #(.enable("false"), .select(4), .width(4)) multiplexer_1 (
    .in0(Reg0_Out), .in1(Reg1_Out), .in2(Reg2_Out), .in3(Reg3_Out), .in4(Reg4_Out), .in5(Reg5_Out),
    .in6(Reg6_Out), .in7(Reg7_Out), .in8(Reg8_Out), .in9(Reg9_Out), .in10(Reg10_Out), .in11(Reg11_Out),
    .in12(Reg12_Out), .in13(Reg13_Out), .in14(Reg14_Out), .in15(Reg15_Out), .out(A_Out), .sel(A_Sel_In));
  Multiplexer #(.enable("false"), .select(4), .width(4)) multiplexer_2 (
    .in0(Reg0_Out), .in1(Reg1_Out), .in2(Reg2_Out), .in3(Reg3_Out), .in4(Reg4_Out), .in5(Reg5_Out),
    .in6(Reg6_Out), .in7(Reg7_Out), .in8(Reg8_Out), .in9(Reg9_Out), .in10(Reg10_Out), .in11(Reg11_Out),
    .in12(Reg12_Out), .in13(Reg13_Out), .in14(Reg14_Out), .in15(Reg15_Out), .out(B_Out), .sel(B_Sel_In));

  // Other names for the same wires on the sheet: A[3:0] = A_Out; A_Sel[3:0] = A_Sel_In; B[3:0] = B_Out;
  //   B_Sel[3:0] = B_Sel_In; C_Sel[3:0] = C_Sel_In; clk = clk_in; Data[3:0] = Data_In; Reg0[3:0] = Reg0_Out;
  //   Reg1[3:0] = Reg1_Out; Reg2[3:0] = Reg2_Out; Reg3[3:0] = Reg3_Out; Reg4[3:0] = Reg4_Out; Reg5[3:0] = Reg5_Out;
  //   Reg6[3:0] = Reg6_Out; Reg7[3:0] = Reg7_Out; Reg8[3:0] = Reg8_Out; Reg9[3:0] = Reg9_Out; Reg10[3:0] = Reg10_Out;
  //   Reg11[3:0] = Reg11_Out; Reg12[3:0] = Reg12_Out; Reg13[3:0] = Reg13_Out; Reg14[3:0] = Reg14_Out;
  //   Reg15[3:0] = Reg15_Out; Reg_Write = Reg_Write_In
endmodule

module PC (
  input  [3:0] in_1,
  input  in_2,
  output out_3,
  output [4:0] out_4,
  output out_5
);

  wire g5;

  Multiplexer #(.enable("false"), .select(4)) multiplexer_1 (
    .in0(1'b0), .in1(1'b0), .in2(1'b1), .in3(1'b1), .in4(1'b1), .in5(1'b1), .in6(1'b1), .in7(1'b1),
    .in8(1'b1), .in9(1'b1), .in10(1'b1), .in11(1'b1), .in12(1'b1), .in13(1'b1), .in14(1'b1), .in15(1'b1),
    .out(out_3), .sel(in_1));
  Multiplexer #(.enable("false"), .select(4)) multiplexer_2 (
    .in0(1'b0), .in1(1'b0), .in2(1'b1), .in3(1'b0), .in4(1'b0), .in5(1'b1), .in6(1'b0), .in7(1'b1),
    .in8(1'b0), .in9(1'b1), .in10(1'b0), .in11(1'b0), .in12(1'b0), .in13(1'b1), .in14(1'b0), .in15(1'b1),
    .out(out_5), .sel(in_1));
  Counter #(.max('h1f), .width(5)) counter_1 (.count(g5), .clk(in_2), .Q(out_4));  // open: clr, load, up, D, carry
  Multiplexer #(.enable("false"), .select(4)) multiplexer_3 (
    .in0(1'b0), .in1(1'b1), .in2(1'b1), .in3(1'b1), .in4(1'b1), .in5(1'b1), .in6(1'b1), .in7(1'b1),
    .in8(1'b1), .in9(1'b1), .in10(1'b1), .in11(1'b1), .in12(1'b1), .in13(1'b1), .in14(1'b1), .in15(1'b1),
    .out(g5), .sel(in_1));

  // Other names for the same wires on the sheet: Clk = in_2; Imm = out_5; Instr[4:0] = out_4; OpCode[3:0] = in_1;
  //   WriteEn = out_3
endmodule

module ALU (
  input  [3:0] in_1,
  input  [3:0] in_2,
  input  [3:0] in_3,
  output [3:0] out_4
);

  wire [3:0] adder_1_out, and_1_out, negator_1_out, not_1_out, or_1_out, subtractor_1_out, xor_1_out;

  assign or_1_out = in_3 | in_2;  // OR_Gate or_1, 4 bits wide
  assign and_1_out = in_3 & in_2;  // AND_Gate and_1, 4 bits wide
  assign xor_1_out = in_3 ^ in_2;  // XOR_Gate xor_1, 4 bits wide
  assign not_1_out = ~in_2;  // NOT_Gate not_1, 4 bits wide
  Negator #(.width(4)) negator_1 (.in(in_2), .out(negator_1_out));
  Adder #(.width(4)) adder_1 (.a(in_2), .b(in_3), .out(adder_1_out));  // open: cin, cout
  Subtractor #(.width(4)) subtractor_1 (.a(in_2), .b(in_3), .out(subtractor_1_out));  // open: bin, bout
  Multiplexer #(.enable("false"), .select(4), .width(4)) multiplexer_1 (
    .in0(4'b0000), .in1(4'b0000), .in2(in_3), .in3(in_2), .in4(and_1_out), .in5(and_1_out), .in6(or_1_out),
    .in7(or_1_out), .in8(xor_1_out), .in9(xor_1_out), .in10(not_1_out), .in11(negator_1_out),
    .in12(adder_1_out), .in13(adder_1_out), .in14(subtractor_1_out), .in15(subtractor_1_out), .out(out_4),
    .sel(in_1));

  // Other names for the same wires on the sheet: AIn[3:0] = in_2; BIn[3:0] = in_3; Result[3:0] = out_4;
  //   Sel[3:0] = in_1
endmodule
